// Digital circuit 1bit_register.dig as structural Verilog
module _1bit_register (
  input  write,
  input  data,
  input  clk,
  output A3
);

  wire multiplexer_1_out;

  Multiplexer multiplexer_1 (.sel(write), .in_0(A3), .in_1(data), .out(multiplexer_1_out));
  D_FF d_ff_1 (.D(multiplexer_1_out), .C(clk), .Q(A3));  // open: nQ
endmodule
