// Digital circuit 4bit_adder.dig as structural Verilog
module _4bit_adder (
  input  C0,
  input  A1,
  input  A2,
  input  A3,
  input  A4,
  input  B1,
  input  B2,
  input  B3,
  input  B4,
  output S1,
  output S2,
  output S3,
  output S4,
  output C4
);

  wire full_adder_1_p5, full_adder_2_p5, full_adder_3_p5;

  // full_adder full_adder_1: pin names not known; wires that end beside it: C0, A1, B1, S1, full_adder_1_p5
  // full_adder full_adder_2: pin names not known; wires that end beside it: full_adder_1_p5, A2, B2, S2, full_adder_2_p5
  // full_adder full_adder_3: pin names not known; wires that end beside it: full_adder_2_p5, A3, B3, S3, full_adder_3_p5
  // full_adder full_adder_4: pin names not known; wires that end beside it: full_adder_3_p5, A4, B4, S4, C4
endmodule
