// Digital circuit D_latch.dig as structural Verilog
module D_latch (
  input  EN,
  input  D,
  output Q
);

  wire nand_1_out, nand_2_out, nand_4_out, not_1_out;

  not not_1 (not_1_out, D);
  nand nand_1 (nand_1_out, D, EN);
  nand nand_2 (nand_2_out, EN, not_1_out);
  nand nand_3 (Q, nand_1_out, nand_4_out);
  nand nand_4 (nand_4_out, Q, nand_2_out);
endmodule
