// Digital circuit fourbit_synch_counter.dig as structural Verilog
module fourbit_synch_counter (
  input  clk,
  input  _1,
  output A0,
  output A1,
  output A2,
  output A3
);

  wire and_1_out, and_2_out;

  T_FF t_ff_1 (.T(_1), .C(clk), .Q(A0));  // open: nQ
  T_FF t_ff_2 (.T(A0), .C(clk), .Q(A1));  // open: nQ
  and and_1 (and_1_out, A0, A1);
  T_FF t_ff_3 (.T(and_1_out), .C(clk), .Q(A2));  // open: nQ
  and and_2 (and_2_out, and_1_out, A2);
  T_FF t_ff_4 (.T(and_2_out), .C(clk), .Q(A3));  // open: nQ

  // Notes on the sheet:
  //   _1: default 1
endmodule
