// Digital circuit shiftregister.dig as structural Verilog
module shiftregister (
  input  D,
  input  Clock,
  output Q1,
  output Q2,
  output Q3,
  output Q4
);

  D_FF d_ff_1 (.D(D), .C(Clock), .Q(Q1));  // open: nQ
  D_FF d_ff_2 (.D(Q1), .C(Clock), .Q(Q2));  // open: nQ
  D_FF d_ff_3 (.D(Q2), .C(Clock), .Q(Q3));  // open: nQ
  D_FF d_ff_4 (.D(Q3), .C(Clock), .Q(Q4));  // open: nQ
endmodule
